// Logisim project retroputer.circ as structural Verilog: 3 circuits, main circuit main
module main (
  output [3:0] OP
);

  Register #(.width(1)) fZ ();  // open: D, en, Q, clk, clr
  Register ALU_OP1_XH ();  // open: D, en, Q, clk, clr
  Register ALU_OP1_XL ();  // open: D, en, Q, clk, clr
  Register #(.width(1)) fC ();  // open: D, en, Q, clk, clr
  Register #(.width(2)) ALU_OP1_SZ ();  // open: D, en, Q, clk, clr
  Register ALU_OP1_L ();  // open: D, en, Q, clk, clr
  Register ALU_OP1_H ();  // open: D, en, Q, clk, clr
  Register #(.width(1)) fV ();  // open: D, en, Q, clk, clr
  Adder adder_1 ();  // open: a, b, out, cin, cout
  Register #(.width(1)) fN ();  // open: D, en, Q, clk, clr
  Subtractor subtractor_1 ();  // open: a, b, out, bin, bout
  Multiplier multiplier_1 ();  // open: a, b, out, cin, cout
  Divider divider_1 ();  // open: a, b, out, upper, rem
  Register ALU_OP2_XH ();  // open: D, en, Q, clk, clr
  Register ALU_OP2_XL ();  // open: D, en, Q, clk, clr
  Register ALU_OP2_L ();  // open: D, en, Q, clk, clr
  Register ALU_OP2_H ();  // open: D, en, Q, clk, clr
  Register #(.width(1)) fEX ();  // open: D, en, Q, clk, clr
  Register #(.width(1)) fID ();  // open: D, en, Q, clk, clr
  Register #(.width(1)) fIS ();  // open: D, en, Q, clk, clr
  Register #(.width(1)) fSS ();  // open: D, en, Q, clk, clr
endmodule

module ALU (
);

  Register #(.width(1)) register_1 ();  // open: D, en, Q, clk, clr
  Register register_2 ();  // open: D, en, Q, clk, clr
  Register register_3 ();  // open: D, en, Q, clk, clr
  Register #(.width(1)) register_4 ();  // open: D, en, Q, clk, clr
  Adder adder_1 ();  // open: a, b, out, cin, cout
  Subtractor subtractor_1 ();  // open: a, b, out, bin, bout
  Register #(.width(2)) OP1_SZ ();  // open: D, en, Q, clk, clr
  Register #(.width(1)) register_5 ();  // open: D, en, Q, clk, clr
  Register register_6 ();  // open: D, en, Q, clk, clr
  Register register_7 ();  // open: D, en, Q, clk, clr
  Register #(.width(1)) register_8 ();  // open: D, en, Q, clk, clr
  Multiplier multiplier_1 ();  // open: a, b, out, cin, cout
  Divider divider_1 ();  // open: a, b, out, upper, rem
  Register register_9 ();  // open: D, en, Q, clk, clr
  Register register_10 ();  // open: D, en, Q, clk, clr
  Register #(.width(2)) register_11 ();  // open: D, en, Q, clk, clr
  Register register_12 ();  // open: D, en, Q, clk, clr
  Register register_13 ();  // open: D, en, Q, clk, clr
  Register #(.width(1)) register_14 ();  // open: D, en, Q, clk, clr

  // Notes on the sheet:
  //   16-Bit ALU
  //   32-Bit ALU
  //   8-Bit ALU
endmodule

module ALU8 (
  input  [7:0] A_IN,
  input  [7:0] B_IN,
  input  C_IN,
  input  [3:0] OP,
  output [7:0] RESULT,
  output C,
  output Z,
  output N,
  output V
);

  wire ADD_C, SUB_C;
  wire [7:0] ADD_RESULT, SUB_RESULT;

  Adder adder_1 (.a(A_IN), .b(B_IN), .out(ADD_RESULT), .cin(C_IN), .cout(ADD_C));
  Subtractor subtractor_1 (.a(A_IN), .b(B_IN), .out(SUB_RESULT), .bin(C_IN), .bout(SUB_C));
  Comparator comparator_1 (.a({N, RESULT[6:0]}), .b({8{1'b0}}), .eq(Z));  // open: gt, lt
  Shifter shifter_1 ();  // open: in, dist, out
  Multiplexer #(.select(4), .width(8), .enable("false")) multiplexer_1 (
    .in0(ADD_RESULT), .in1(SUB_RESULT), .out({N, RESULT[6:0]}), .sel(OP));  // open: in2, in3, in4, in5, in6, in7, in8, in9, in10, in11, in12, in13, in14, in15
  Multiplexer #(.select(4), .enable("false")) multiplexer_2 (
    .in0(ADD_C), .in1(SUB_C), .out(C), .sel(OP));  // open: in2, in3, in4, in5, in6, in7, in8, in9, in10, in11, in12, in13, in14, in15

  assign RESULT[7] = N;
endmodule
